// Logisim project Logic Circuit.circ as structural Verilog: 19 circuits, main circuit Circuit logique interne du coffre
module Circuit_logique_interne_du_coffre (
  input  I1,
  input  I2,
  input  I3,
  input  I4,
  output S1,
  output S2,
  output S3,
  output S4
);

  wire and_1_out, and_2_out, and_3_out, and_4_out, and_5_out, and_6_out, and_7_out, and_8_out, and_9_out,
       and_10_out, and_11_out, and_12_out, and_13_out, and_14_out, not_1_out, not_2_out, not_3_out,
       not_4_out, not_5_out, not_6_out, not_7_out, not_8_out, not_9_out, not_10_out, not_11_out, not_12_out,
       not_13_out, not_14_out, not_15_out, not_16_out, not_17_out, not_18_out, not_19_out, not_20_out;

  not not_1 (not_1_out, I2);
  not not_2 (not_2_out, I2);
  not not_3 (not_3_out, I1);
  not not_4 (not_4_out, I4);
  not not_5 (not_5_out, I1);
  not not_6 (not_6_out, I3);
  not not_7 (not_7_out, I2);
  not not_8 (not_8_out, I3);
  not not_9 (not_9_out, I3);
  not not_10 (not_10_out, I4);
  not not_11 (not_11_out, I2);
  not not_12 (not_12_out, I3);
  not not_13 (not_13_out, I4);
  not not_14 (not_14_out, I1);
  not not_15 (not_15_out, I3);
  not not_16 (not_16_out, I4);
  not not_17 (not_17_out, I1);
  not not_18 (not_18_out, I2);
  not not_19 (not_19_out, I3);
  not not_20 (not_20_out, I4);
  and and_1 (and_1_out, not_1_out, I3, I4);
  or or_1 (S1, and_1_out, and_2_out);
  and and_2 (and_2_out, I1, not_2_out, I3);
  and and_3 (and_3_out, not_3_out, I3, not_4_out);
  and and_4 (and_4_out, not_5_out, I2, not_6_out, I4);
  and and_5 (and_5_out, I1, not_7_out, not_8_out, I4);
  and and_6 (and_6_out, I1, I2, not_9_out, not_10_out);
  and and_7 (and_7_out, I1, I2, I3, I4);
  and and_8 (and_8_out, not_11_out, not_12_out, not_13_out);
  and and_9 (and_9_out, not_14_out, I2);
  and and_10 (and_10_out, I2, not_15_out, I4);
  and and_11 (and_11_out, I2, I3, not_16_out);
  and and_12 (and_12_out, not_17_out, not_18_out);
  or or_2 (S4, and_12_out, and_13_out, and_14_out);
  and and_13 (and_13_out, not_19_out, not_20_out);
  and and_14 (and_14_out, I1, I2, I3, I4);
  or or_3 (S2, and_3_out, and_4_out, and_5_out, and_6_out, and_7_out);
  or or_4 (S3, and_8_out, and_9_out, and_10_out, and_11_out);
endmodule

module carte (
  input  I1,
  input  I1_2,
  input  I1_3,
  input  I1_4,
  input  I2,
  input  I2_2,
  input  I2_3,
  input  I2_4,
  input  I3,
  input  I3_2,
  input  I3_3,
  input  I3_4,
  input  I4,
  input  I4_2,
  input  I4_3,
  input  I4_4,
  input  I1_5,
  input  I1_6,
  input  I1_7,
  input  I1_8,
  input  I2_5,
  input  I2_6,
  input  I2_7,
  input  I2_8,
  input  I3_5,
  input  I3_6,
  input  I3_7,
  input  I3_8,
  input  I4_5,
  input  I4_6,
  input  I4_7,
  input  I4_8,
  input  I1_9,
  input  I1_10,
  input  I1_11,
  input  I1_12,
  input  I2_9,
  input  I2_10,
  input  I2_11,
  input  I2_12,
  input  I3_9,
  input  I3_10,
  input  I3_11,
  input  I3_12,
  input  I4_9,
  input  I4_10,
  input  I4_11,
  input  I4_12,
  input  I1_13,
  input  I1_14,
  input  I1_15,
  input  I1_16,
  input  I2_13,
  input  I2_14,
  input  I2_15,
  input  I2_16,
  input  I3_13,
  input  I3_14,
  input  I3_15,
  input  I3_16,
  input  I4_13,
  input  I4_14,
  input  I4_15,
  input  I4_16,
  output out_65,
  output out_66,
  output out_67,
  output out_68,
  output out_69,
  output out_70,
  output out_71,
  output out_72,
  output out_73,
  output out_74,
  output out_75,
  output out_76,
  output out_77,
  output out_78,
  output out_79,
  output out_80,
  output out_81,
  output out_82,
  output out_83,
  output out_84,
  output out_85,
  output out_86,
  output out_87,
  output out_88,
  output out_89,
  output out_90,
  output out_91,
  output out_92,
  output out_93,
  output out_94,
  output out_95,
  output out_96,
  output out_97,
  output out_98,
  output out_99,
  output out_100,
  output out_101,
  output out_102,
  output out_103,
  output out_104,
  output out_105,
  output out_106,
  output out_107,
  output out_108,
  output out_109,
  output out_110,
  output out_111,
  output out_112,
  output out_113,
  output out_114,
  output out_115,
  output out_116,
  output out_117,
  output out_118,
  output out_119,
  output out_120,
  output out_121,
  output out_122,
  output out_123,
  output out_124,
  output out_125,
  output out_126,
  output out_127,
  output out_128
);

  wire not_1_out, not_2_out, not_3_out, not_4_out, not_5_out, not_6_out, not_7_out, not_8_out, not_9_out,
       not_10_out, not_11_out, not_12_out, not_13_out, not_14_out, not_15_out, not_16_out, not_17_out,
       not_18_out, not_19_out, not_20_out, not_21_out, not_22_out, not_23_out, not_24_out, not_25_out,
       not_26_out, not_27_out, not_28_out, not_29_out, not_30_out, not_31_out, not_32_out;

  not not_1 (not_1_out, I2);
  not not_2 (not_2_out, I4);
  not not_3 (not_3_out, I2_5);
  not not_4 (not_4_out, I1_12);
  not not_5 (not_5_out, I2_12);
  not not_6 (not_6_out, I3_12);
  not not_7 (not_7_out, I1_16);
  and and_1 (out_65, I1, not_1_out, I3, not_2_out);
  and and_2 (out_81, I1_5, not_3_out, I3_5, I4_5);
  and and_3 (out_112, not_4_out, not_5_out, not_6_out, I4_12);
  and and_4 (out_124, not_7_out, I2_16, I3_16, I4_16);
  D_Flip_Flop d_ff_1 (.clk(out_65), .Q(out_69));  // open: D, Qn, preset, en, reset
  D_Flip_Flop d_ff_2 (.clk(out_65), .Q(out_73));  // open: D, Qn, preset, en, reset
  D_Flip_Flop d_ff_3 (.clk(out_65), .Q(out_77));  // open: D, Qn, preset, en, reset
  D_Flip_Flop d_ff_4 (.clk(out_81), .Q(out_85));  // open: D, Qn, preset, en, reset
  D_Flip_Flop d_ff_5 (.clk(out_81), .Q(out_89));  // open: D, Qn, preset, en, reset
  D_Flip_Flop d_ff_6 (.clk(out_81), .Q(out_93));  // open: D, Qn, preset, en, reset
  D_Flip_Flop d_ff_7 (.clk(out_112), .Q(out_100));  // open: D, Qn, preset, en, reset
  D_Flip_Flop d_ff_8 (.clk(out_112), .Q(out_104));  // open: D, Qn, preset, en, reset
  D_Flip_Flop d_ff_9 (.clk(out_112), .Q(out_108));  // open: D, Qn, preset, en, reset
  D_Flip_Flop d_ff_10 (.clk(out_124), .Q(out_116));  // open: D, Qn, preset, en, reset
  D_Flip_Flop d_ff_11 (.clk(out_124), .Q(out_120));  // open: D, Qn, preset, en, reset
  D_Flip_Flop d_ff_12 (.clk(out_124), .Q(out_128));  // open: D, Qn, preset, en, reset
  not not_8 (not_8_out, I3_2);
  not not_9 (not_9_out, I4_6);
  not not_10 (not_10_out, I1_9);
  not not_11 (not_11_out, I2_9);
  not not_12 (not_12_out, I3_9);
  not not_13 (not_13_out, I4_9);
  not not_14 (not_14_out, I2_13);
  not not_15 (not_15_out, I3_13);
  not not_16 (not_16_out, I4_13);
  and and_5 (out_74, I1_2, I2_2, not_8_out, I4_2);
  and and_6 (out_90, I1_6, I2_6, I3_6, not_9_out);
  and and_7 (out_105, not_10_out, not_11_out, not_12_out, not_13_out);
  and and_8 (out_121, I1_13, not_14_out, not_15_out, not_16_out);
  D_Flip_Flop d_ff_13 (.clk(out_74), .Q(out_66));  // open: D, Qn, preset, en, reset
  D_Flip_Flop d_ff_14 (.clk(out_74), .Q(out_70));  // open: D, Qn, preset, en, reset
  D_Flip_Flop d_ff_15 (.clk(out_74), .Q(out_78));  // open: D, Qn, preset, en, reset
  D_Flip_Flop d_ff_16 (.clk(out_90), .Q(out_82));  // open: D, Qn, preset, en, reset
  D_Flip_Flop d_ff_17 (.clk(out_90), .Q(out_86));  // open: D, Qn, preset, en, reset
  D_Flip_Flop d_ff_18 (.clk(out_90), .Q(out_94));  // open: D, Qn, preset, en, reset
  D_Flip_Flop d_ff_19 (.clk(out_105), .Q(out_97));  // open: D, Qn, preset, en, reset
  D_Flip_Flop d_ff_20 (.clk(out_105), .Q(out_101));  // open: D, Qn, preset, en, reset
  D_Flip_Flop d_ff_21 (.clk(out_121), .Q(out_113));  // open: D, Qn, preset, en, reset
  D_Flip_Flop d_ff_22 (.clk(out_121), .Q(out_117));  // open: D, Qn, preset, en, reset
  not not_17 (not_17_out, I1_3);
  not not_18 (not_18_out, I3_3);
  not not_19 (not_19_out, I4_3);
  not not_20 (not_20_out, I2_7);
  not not_21 (not_21_out, I3_7);
  not not_22 (not_22_out, I1_10);
  not not_23 (not_23_out, I2_10);
  not not_24 (not_24_out, I4_10);
  not not_25 (not_25_out, I3_14);
  not not_26 (not_26_out, I4_14);
  and and_9 (out_75, not_17_out, I2_3, not_18_out, not_19_out);
  and and_10 (out_87, I1_7, not_20_out, not_21_out, I4_7);
  and and_11 (out_102, not_22_out, not_23_out, I3_10, not_24_out);
  and and_12 (out_118, I1_14, I2_14, not_25_out, not_26_out);
  D_Flip_Flop d_ff_23 (.clk(out_75), .Q(out_67));  // open: D, Qn, preset, en, reset
  D_Flip_Flop d_ff_24 (.clk(out_75), .Q(out_71));  // open: D, Qn, preset, en, reset
  D_Flip_Flop d_ff_25 (.clk(out_87), .Q(out_83));  // open: D, Qn, preset, en, reset
  D_Flip_Flop d_ff_26 (.clk(out_87), .Q(out_91));  // open: D, Qn, preset, en, reset
  D_Flip_Flop d_ff_27 (.clk(out_87), .Q(out_95));  // open: D, Qn, preset, en, reset
  D_Flip_Flop d_ff_28 (.clk(out_102), .Q(out_98));  // open: D, Qn, preset, en, reset
  D_Flip_Flop d_ff_29 (.clk(out_102), .Q(out_106));  // open: D, Qn, preset, en, reset
  D_Flip_Flop d_ff_30 (.clk(out_118), .Q(out_114));  // open: D, Qn, preset, en, reset
  D_Flip_Flop d_ff_31 (.clk(out_118), .Q(out_122));  // open: D, Qn, preset, en, reset
  not not_27 (not_27_out, I1_8);
  not not_28 (not_28_out, I3_8);
  not not_29 (not_29_out, I1_11);
  not not_30 (not_30_out, I4_11);
  not not_31 (not_31_out, I1_15);
  not not_32 (not_32_out, I2_15);
  and and_13 (out_72, I1_4, I2_4, I3_4, I4_4);
  and and_14 (out_88, not_27_out, I2_8, not_28_out, I4_8);
  and and_15 (out_103, not_29_out, I2_11, I3_11, not_30_out);
  and and_16 (out_115, not_31_out, not_32_out, I3_15, I4_15);
  D_Flip_Flop d_ff_32 (.clk(out_72), .Q(out_68));  // open: D, Qn, preset, en, reset
  D_Flip_Flop d_ff_33 (.clk(out_72), .Q(out_76));  // open: D, Qn, preset, en, reset
  D_Flip_Flop d_ff_34 (.clk(out_88), .Q(out_84));  // open: D, Qn, preset, en, reset
  D_Flip_Flop d_ff_35 (.clk(out_88), .Q(out_96));  // open: D, Qn, preset, en, reset
  D_Flip_Flop d_ff_36 (.clk(out_103), .Q(out_99));  // open: D, Qn, preset, en, reset
  D_Flip_Flop d_ff_37 (.clk(out_103), .Q(out_111));  // open: D, Qn, preset, en, reset
  D_Flip_Flop d_ff_38 (.clk(out_115), .Q(out_119));  // open: D, Qn, preset, en, reset
  D_Flip_Flop d_ff_39 (.clk(out_115), .Q(out_123));  // open: D, Qn, preset, en, reset

  assign out_79 = out_75;
  assign out_80 = out_72;
  assign out_92 = out_88;
  assign out_107 = out_103;
  assign out_109 = out_105;
  assign out_110 = out_102;
  assign out_125 = out_121;
  assign out_126 = out_118;
  assign out_127 = out_115;

  // Notes on the sheet:
  //   Modèle 1 carte 1
  //   Modèle 1 carte 2
  //   Modèle 2 carte 1
  //   Modèle 3 carte 1
  //   Modèle 3 carte 2
  //   Modèle 3 carte 3
  //   Modèle 4 carte 1
  //   Modèle 4 carte 2
  //   Modèle 4 carte 3
  //   Modèle 5 carte 1
  //   Modèle 6 carte 1
  //   Modèle 6 carte 2
  //   Modèle 6 carte 3
  //   Modèle 7 carte 1
  //   Modèle 7 carte 2
  //   Modèle 8 carte 1
endmodule

module comparateur (
  input  I1,
  input  I2,
  input  I3,
  input  I4,
  output out_5
);

  wire circuit_logique_interne_du_coffre_1_s1, circuit_logique_interne_du_coffre_1_s2,
       circuit_logique_interne_du_coffre_1_s3, circuit_logique_interne_du_coffre_1_s4,
       \modèle_8_carte_1_1_out_5 , \modèle_8_carte_1_1_out_6 , \modèle_8_carte_1_1_out_7 ,
       \modèle_8_carte_1_1_out_8 , xnor_1_out, xnor_2_out, xnor_3_out, xnor_4_out;

  Circuit_logique_interne_du_coffre circuit_logique_interne_du_coffre_1 (
    .I1(I1), .I2(I2), .I3(I3), .I4(I4), .S1(circuit_logique_interne_du_coffre_1_s1),
    .S2(circuit_logique_interne_du_coffre_1_s2), .S3(circuit_logique_interne_du_coffre_1_s3),
    .S4(circuit_logique_interne_du_coffre_1_s4));
  \Modèle_8_carte_1  \modèle_8_carte_1_1  (
    .I1(I1), .I2(I2), .I3(I3), .I4(I4), .out_5(\modèle_8_carte_1_1_out_5 ),
    .out_6(\modèle_8_carte_1_1_out_6 ), .out_7(\modèle_8_carte_1_1_out_7 ), .out_8(\modèle_8_carte_1_1_out_8 ));
  xnor xnor_1 (xnor_1_out, circuit_logique_interne_du_coffre_1_s1, \modèle_8_carte_1_1_out_5 );
  xnor xnor_2 (xnor_2_out, circuit_logique_interne_du_coffre_1_s2, \modèle_8_carte_1_1_out_6 );
  xnor xnor_3 (xnor_3_out, circuit_logique_interne_du_coffre_1_s3, \modèle_8_carte_1_1_out_7 );
  xnor xnor_4 (xnor_4_out, circuit_logique_interne_du_coffre_1_s4, \modèle_8_carte_1_1_out_8 );
  and and_1 (out_5, xnor_1_out, xnor_2_out, xnor_3_out, xnor_4_out);
endmodule

module \Modèle_1_carte_1  (
  input  I1,
  input  I2,
  input  I3,
  input  I4,
  output out_5,
  output out_6,
  output out_7,
  output out_8
);

  wire not_1_out, not_2_out;

  not not_1 (not_1_out, I2);
  not not_2 (not_2_out, I4);
  and and_1 (out_5, I1, not_1_out, I3, not_2_out);
  D_Flip_Flop d_ff_1 (.clk(out_5), .Q(out_6));  // open: D, Qn, preset, en, reset
  D_Flip_Flop d_ff_2 (.clk(out_5), .Q(out_7));  // open: D, Qn, preset, en, reset
  D_Flip_Flop d_ff_3 (.clk(out_5), .Q(out_8));  // open: D, Qn, preset, en, reset

  // Notes on the sheet:
  //   Modèle 1 carte 1
endmodule

module \Modèle_1_carte_2  (
  input  I1,
  input  I2,
  input  I3,
  input  I4,
  output out_5,
  output out_6,
  output out_7,
  output out_8
);

  wire not_1_out;

  not not_1 (not_1_out, I2);
  and and_1 (out_5, I1, not_1_out, I3, I4);
  D_Flip_Flop d_ff_1 (.clk(out_5), .Q(out_6));  // open: D, Qn, preset, en, reset
  D_Flip_Flop d_ff_2 (.clk(out_5), .Q(out_7));  // open: D, Qn, preset, en, reset
  D_Flip_Flop d_ff_3 (.clk(out_5), .Q(out_8));  // open: D, Qn, preset, en, reset

  // Notes on the sheet:
  //   Modèle 1 carte 2
endmodule

module \Modèle_2_carte_1  (
  input  I1,
  input  I2,
  input  I3,
  input  I4,
  output out_5,
  output out_6,
  output out_7,
  output out_8
);

  wire not_1_out, not_2_out, not_3_out;

  not not_1 (not_1_out, I1);
  not not_2 (not_2_out, I2);
  not not_3 (not_3_out, I3);
  and and_1 (out_8, not_1_out, not_2_out, not_3_out, I4);
  D_Flip_Flop d_ff_1 (.clk(out_8), .Q(out_5));  // open: D, Qn, preset, en, reset
  D_Flip_Flop d_ff_2 (.clk(out_8), .Q(out_6));  // open: D, Qn, preset, en, reset
  D_Flip_Flop d_ff_3 (.clk(out_8), .Q(out_7));  // open: D, Qn, preset, en, reset

  // Notes on the sheet:
  //   Modèle 2 carte 1
endmodule

module \Modèle_3_carte_1  (
  input  I1,
  input  I2,
  input  I3,
  input  I4,
  output out_5,
  output out_6,
  output out_7,
  output out_8
);

  wire not_1_out;

  not not_1 (not_1_out, I1);
  and and_1 (out_7, not_1_out, I2, I3, I4);
  D_Flip_Flop d_ff_1 (.clk(out_7), .Q(out_5));  // open: D, Qn, preset, en, reset
  D_Flip_Flop d_ff_2 (.clk(out_7), .Q(out_6));  // open: D, Qn, preset, en, reset
  D_Flip_Flop d_ff_3 (.clk(out_7), .Q(out_8));  // open: D, Qn, preset, en, reset

  // Notes on the sheet:
  //   Modèle 3 carte 1
endmodule

module \Modèle_3_carte_2  (
  input  I1,
  input  I2,
  input  I3,
  input  I4,
  output out_5,
  output out_6,
  output out_7,
  output out_8
);

  wire not_1_out;

  not not_1 (not_1_out, I3);
  and and_1 (out_7, I1, I2, not_1_out, I4);
  D_Flip_Flop d_ff_1 (.clk(out_7), .Q(out_5));  // open: D, Qn, preset, en, reset
  D_Flip_Flop d_ff_2 (.clk(out_7), .Q(out_6));  // open: D, Qn, preset, en, reset
  D_Flip_Flop d_ff_3 (.clk(out_7), .Q(out_8));  // open: D, Qn, preset, en, reset

  // Notes on the sheet:
  //   Modèle 3 carte 2
endmodule

module \Modèle_3_carte_3  (
  input  I1,
  input  I2,
  input  I3,
  input  I4,
  output out_5,
  output out_6,
  output out_7,
  output out_8
);

  wire not_1_out;

  not not_1 (not_1_out, I4);
  and and_1 (out_7, I1, I2, I3, not_1_out);
  D_Flip_Flop d_ff_1 (.clk(out_7), .Q(out_5));  // open: D, Qn, preset, en, reset
  D_Flip_Flop d_ff_2 (.clk(out_7), .Q(out_6));  // open: D, Qn, preset, en, reset
  D_Flip_Flop d_ff_3 (.clk(out_7), .Q(out_8));  // open: D, Qn, preset, en, reset

  // Notes on the sheet:
  //   Modèle 3 carte 3
endmodule

module \Modèle_4_carte_1  (
  input  I1,
  input  I2,
  input  I3,
  input  I4,
  output out_5,
  output out_6,
  output out_7,
  output out_8
);

  wire not_1_out, not_2_out, not_3_out, not_4_out;

  not not_1 (not_1_out, I1);
  not not_2 (not_2_out, I2);
  not not_3 (not_3_out, I3);
  not not_4 (not_4_out, I4);
  and and_1 (out_7, not_1_out, not_2_out, not_3_out, not_4_out);
  D_Flip_Flop d_ff_1 (.clk(out_7), .Q(out_5));  // open: D, Qn, preset, en, reset
  D_Flip_Flop d_ff_2 (.clk(out_7), .Q(out_6));  // open: D, Qn, preset, en, reset

  assign out_8 = out_7;

  // Notes on the sheet:
  //   Modèle 4 carte 1
endmodule

module \Modèle_4_carte_2  (
  input  I1,
  input  I2,
  input  I3,
  input  I4,
  output out_5,
  output out_6,
  output out_7,
  output out_8
);

  wire not_1_out, not_2_out, not_3_out;

  not not_1 (not_1_out, I2);
  not not_2 (not_2_out, I3);
  not not_3 (not_3_out, I4);
  and and_1 (out_7, I1, not_1_out, not_2_out, not_3_out);
  D_Flip_Flop d_ff_1 (.clk(out_7), .Q(out_5));  // open: D, Qn, preset, en, reset
  D_Flip_Flop d_ff_2 (.clk(out_7), .Q(out_6));  // open: D, Qn, preset, en, reset

  assign out_8 = out_7;

  // Notes on the sheet:
  //   Modèle 4 carte 2
endmodule

module \Modèle_4_carte_3  (
  input  I1,
  input  I2,
  input  I3,
  input  I4,
  output out_5,
  output out_6,
  output out_7,
  output out_8
);

  wire not_1_out, not_2_out, not_3_out;

  not not_1 (not_1_out, I1);
  not not_2 (not_2_out, I3);
  not not_3 (not_3_out, I4);
  and and_1 (out_7, not_1_out, I2, not_2_out, not_3_out);
  D_Flip_Flop d_ff_1 (.clk(out_7), .Q(out_5));  // open: D, Qn, preset, en, reset
  D_Flip_Flop d_ff_2 (.clk(out_7), .Q(out_6));  // open: D, Qn, preset, en, reset

  assign out_8 = out_7;

  // Notes on the sheet:
  //   Modèle 4 carte 3
endmodule

module \Modèle_5_carte_1  (
  input  I1,
  input  I2,
  input  I3,
  input  I4,
  output out_5,
  output out_6,
  output out_7,
  output out_8
);

  wire not_1_out, not_2_out;

  not not_1 (not_1_out, I2);
  not not_2 (not_2_out, I3);
  and and_1 (out_6, I1, not_1_out, not_2_out, I4);
  D_Flip_Flop d_ff_1 (.clk(out_6), .Q(out_5));  // open: D, Qn, preset, en, reset
  D_Flip_Flop d_ff_2 (.clk(out_6), .Q(out_7));  // open: D, Qn, preset, en, reset
  D_Flip_Flop d_ff_3 (.clk(out_6), .Q(out_8));  // open: D, Qn, preset, en, reset

  // Notes on the sheet:
  //   Modèle 5 carte 1
endmodule

module \Modèle_6_carte_1  (
  input  I1,
  input  I2,
  input  I3,
  input  I4,
  output out_5,
  output out_6,
  output out_7,
  output out_8
);

  wire not_1_out, not_2_out, not_3_out;

  not not_1 (not_1_out, I1);
  not not_2 (not_2_out, I2);
  not not_3 (not_3_out, I4);
  and and_1 (out_6, not_1_out, not_2_out, I3, not_3_out);
  D_Flip_Flop d_ff_1 (.clk(out_6), .Q(out_5));  // open: D, Qn, preset, en, reset
  D_Flip_Flop d_ff_2 (.clk(out_6), .Q(out_7));  // open: D, Qn, preset, en, reset

  assign out_8 = out_6;

  // Notes on the sheet:
  //   Modèle 6 carte 1
endmodule

module \Modèle_6_carte_2  (
  input  I1,
  input  I2,
  input  I3,
  input  I4,
  output out_5,
  output out_6,
  output out_7,
  output out_8
);

  wire not_1_out, not_2_out;

  not not_1 (not_1_out, I3);
  not not_2 (not_2_out, I4);
  and and_1 (out_6, I1, I2, not_1_out, not_2_out);
  D_Flip_Flop d_ff_1 (.clk(out_6), .Q(out_5));  // open: D, Qn, preset, en, reset
  D_Flip_Flop d_ff_2 (.clk(out_6), .Q(out_7));  // open: D, Qn, preset, en, reset

  assign out_8 = out_6;

  // Notes on the sheet:
  //   Modèle 6 carte 2
endmodule

module \Modèle_6_carte_3  (
  input  I1,
  input  I2,
  input  I3,
  input  I4,
  output out_5,
  output out_6,
  output out_7,
  output out_8
);

  and and_1 (out_6, I1, I2, I3, I4);
  D_Flip_Flop d_ff_1 (.clk(out_6), .Q(out_5));  // open: D, Qn, preset, en, reset
  D_Flip_Flop d_ff_2 (.clk(out_6), .Q(out_7));  // open: D, Qn, preset, en, reset

  assign out_8 = out_6;

  // Notes on the sheet:
  //   Modèle 6 carte 3
endmodule

module \Modèle_7_carte_1  (
  input  I1,
  input  I2,
  input  I3,
  input  I4,
  output out_5,
  output out_6,
  output out_7,
  output out_8
);

  wire not_1_out, not_2_out;

  not not_1 (not_1_out, I1);
  not not_2 (not_2_out, I3);
  and and_1 (out_6, not_1_out, I2, not_2_out, I4);
  D_Flip_Flop d_ff_1 (.clk(out_6), .Q(out_5));  // open: D, Qn, preset, en, reset
  D_Flip_Flop d_ff_2 (.clk(out_6), .Q(out_8));  // open: D, Qn, preset, en, reset

  assign out_7 = out_6;

  // Notes on the sheet:
  //   Modèle 7 carte 1
endmodule

module \Modèle_7_carte_2  (
  input  I1,
  input  I2,
  input  I3,
  input  I4,
  output out_5,
  output out_6,
  output out_7,
  output out_8
);

  wire not_1_out, not_2_out;

  not not_1 (not_1_out, I1);
  not not_2 (not_2_out, I4);
  and and_1 (out_6, not_1_out, I2, I3, not_2_out);
  D_Flip_Flop d_ff_1 (.clk(out_6), .Q(out_5));  // open: D, Qn, preset, en, reset
  D_Flip_Flop d_ff_2 (.clk(out_6), .Q(out_8));  // open: D, Qn, preset, en, reset

  assign out_7 = out_6;

  // Notes on the sheet:
  //   Modèle 7 carte 2
endmodule

module \Modèle_8_carte_1  (
  input  I1,
  input  I2,
  input  I3,
  input  I4,
  output out_5,
  output out_6,
  output out_7,
  output out_8
);

  wire not_1_out, not_2_out;

  not not_1 (not_1_out, I1);
  not not_2 (not_2_out, I2);
  and and_1 (out_5, not_1_out, not_2_out, I3, I4);
  D_Flip_Flop d_ff_1 (.clk(out_5), .Q(out_6));  // open: D, Qn, preset, en, reset
  D_Flip_Flop d_ff_2 (.clk(out_5), .Q(out_7));  // open: D, Qn, preset, en, reset

  assign out_8 = out_5;

  // Notes on the sheet:
  //   Modèle 8 carte 1
endmodule
